# Fritzing sketch CanonRemote (saved by Fritzing 0.9.3b)
circuit board: 8.46667cm x 5.64444cm
breadboards: 1

parts:
  Bauteil1 = Arduino Uno (Rev3)
  U1 = Sharp PC847X [package=THT]
  R1 = Resistor [tolerance=±5% resistance=220 package=THT]
  LED1 = LED - 5mm [color="Red (633nm)" package="5 mm [THT]"]
  LED2 = LED - 5mm [color="Green (565nm)" package="5 mm [THT]"]
  R2 = Resistor [tolerance=±5% resistance=220 package=THT]
  J1 = screw terminal, 3 pins

nets:
  N1: Bauteil1.GND, U1.Pin_2, U1.Pin_6
  N2: Bauteil1.D6_PWM, R2.Pin_1
  N3: Bauteil1.D7, R1.Pin_1
  N4: U1.Pin_1, LED1.cathode
  N5: U1.Pin_5, LED2.cathode
  N6: U1.Pin_11, U1.Pin_15, J1.pin2
  N7: U1.Pin_12, J1.pin3
  N8: U1.Pin_16, J1.pin1
  N9: R1.Pin_0, LED2.anode
  N10: LED1.anode, R2.Pin_0

notes:
  focus
  ground
  shutter release
