# Fritzing sketch Interrupt_01 (saved by Fritzing 0.9.3b)
circuit board: 8.46667cm x 5.64444cm
breadboards: 1

parts:
  Bauteil1 = Arduino Uno (Rev3)
  S1 = Pushbutton [package=THT]
  R1 = Resistor [tolerance=±5% resistance=10k package=THT]

nets:
  N1: Bauteil1.D2, S1.leg1, R1.Pin_1
  N2: Bauteil1.5V, S1.leg0
  N3: Bauteil1.GND, R1.Pin_0
